// Logisim project control_logic_mine_failed.circ as structural Verilog: 12 circuits, main circuit control_logic
module control_logic (
  input  [31:0] inst,
  input  BrEq,
  input  BrLt,
  output PCSel,
  output RegWEn,
  output [2:0] ImmSel,
  output BrUn,
  output ASel,
  output BSel,
  output [3:0] ALUSel,
  output MemRW,
  output [1:0] WBSel,
  output BrSel,
  output AddrSel
);

  RegWEn_processor regwen_processor_1 (.Opcode(inst[6:0]), .RegWEn(RegWEn));
  ASel_processor asel_processor_1 (.Opcode(inst[6:0]), .ASel(ASel));
  MemRW_processor memrw_processor_1 (.Opcode(inst[6:0]), .funct3(inst[14:12]), .BrEq(BrEq), .BrLt(BrLt), .MemRW(MemRW));
  WBSel_processor wbsel_processor_1 (.Opcode(inst[6:0]), .funct3(inst[14:12]), .WBSel(WBSel));
  ALUSel_processor alusel_processor_1 (.Opcode(inst[6:0]), .funct3(inst[14:12]), .funct7(inst[31:25]), .ALUSel(ALUSel));
  AddrSel_processor addrsel_processor_1 (
    .Opcode(inst[6:0]), .funct3(inst[14:12]), .BrEq(BrEq), .BrLt(BrLt), .AddrSel(AddrSel));
  BrUn_processor brun_processor_1 (.Opcode(inst[6:0]), .funct3(inst[14:12]), .BrUn(BrUn));
  BSel_processor bsel_processor_1 (.Opcode(inst[6:0]), .BSel(BSel));
  PCSel_processor pcsel_processor_1 (.Opcode(inst[6:0]), .funct3(inst[14:12]), .BrEq(BrEq), .BrLt(BrLt), .PCSel(PCSel));
  BrSel_processor brsel_processor_1 (.Opcode(inst[6:0]), .funct3(inst[14:12]), .BrSel(BrSel));
  ImmSel_processor immsel_processor_1 (.Opcode(inst[6:0]), .funct3(inst[14:12]), .ImmSel(ImmSel));

  // Other names for the same wires on the sheet: Opcode[6:0] = inst[6:0]; funct3[2:0] = inst[14:12];
  //   funct7[6:0] = inst[31:25]

  // Notes on the sheet:
  //   INPUTS to your circuit
  //   DON'T CHANGE THE LOCATIONS OF THE INPUTS AND OUTPUTS!
  //   OUTPUT from your circuit
endmodule

module PCSel_processor (
  input  [6:0] Opcode,
  input  [2:0] funct3,
  input  BrEq,
  input  BrLt,
  output PCSel
);

  wire funct3_000, funct3_001, funct3_100, funct3_101, funct3_110, funct3_111, or_1_out, PCSel_B;

  Multiplexer #(.select(2), .enable("false")) multiplexer_1 (
    .in0(1'b0), .in1(1'b0), .in2(1'b1), .out(funct3_000), .sel({BrEq, BrLt}));  // open: in3
  Multiplexer #(.select(2), .enable("false")) multiplexer_2 (
    .in0(1'b1), .in1(1'b0), .in2(1'b1), .out(funct3_101), .sel({BrEq, BrLt}));  // open: in3
  or or_1 (or_1_out, Opcode[2], PCSel_B);
  and and_1 (PCSel, Opcode[6], or_1_out);
  Multiplexer #(.select(2), .enable("false")) multiplexer_3 (
    .in0(1'b1), .in1(1'b1), .in2(1'b0), .out(funct3_001), .sel({BrEq, BrLt}));  // open: in3
  Multiplexer #(.select(2), .enable("false")) multiplexer_4 (
    .in0(1'b0), .in1(1'b1), .in2(1'b0), .out(funct3_110), .sel({BrEq, BrLt}));  // open: in3
  Multiplexer #(.select(3), .enable("false")) multiplexer_5 (
    .in0(funct3_000), .in1(funct3_001), .in4(funct3_100), .in5(funct3_101), .in6(funct3_110),
    .in7(funct3_111), .out(PCSel_B), .sel(funct3));  // open: in2, in3
  Multiplexer #(.select(2), .enable("false")) multiplexer_6 (
    .in0(1'b0), .in1(1'b1), .in2(1'b0), .out(funct3_100), .sel({BrEq, BrLt}));  // open: in3
  Multiplexer #(.select(2), .enable("false")) multiplexer_7 (
    .in0(1'b1), .in1(1'b0), .in2(1'b1), .out(funct3_111), .sel({BrEq, BrLt}));  // open: in3

  // Other names for the same wires on the sheet: Br[1:0] = {BrEq, BrLt}

  // Notes on the sheet:
  //   INPUT
  //   OUTPUT
endmodule

module RegWEn_processor (
  input  [6:0] Opcode,
  output RegWEn
);

  wire and_1_out, not_1_out, not_2_out, not_3_out;

  not not_1 (not_1_out, Opcode[2]);
  not not_2 (not_2_out, Opcode[3]);
  not not_3 (not_3_out, Opcode[4]);
  and and_1 (and_1_out, not_1_out, not_2_out, not_3_out, Opcode[5]);
  not not_4 (RegWEn, and_1_out);

  // Notes on the sheet:
  //   INPUT
  //   OUTPUT
endmodule

module ImmSel_processor (
  input  [6:0] Opcode,
  input  [2:0] funct3,
  output [2:0] ImmSel
);

  wire and_8_out, and_9_out, and_10_out, B_010, I_000, IR_101, is_I_load, is_I_load_or_IR, is_J, is_jalr,
       is_S, is_U, not_1_out, not_2_out, not_3_out, not_4_out, not_5_out, not_6_out, not_7_out, not_8_out,
       not_9_out, not_10_out, not_11_out, not_12_out, not_13_out, not_14_out, not_15_out, not_16_out,
       not_17_out, not_18_out, not_19_out, not_20_out, not_21_out, not_22_out, not_23_out, not_24_out;
  wire [2:0] bitfinder_1_index;

  not not_1 (not_1_out, Opcode[2]);
  not not_2 (not_2_out, Opcode[3]);
  not not_3 (not_3_out, Opcode[4]);
  not not_4 (not_4_out, Opcode[6]);
  not not_5 (not_5_out, Opcode[2]);
  not not_6 (not_6_out, Opcode[3]);
  not not_7 (not_7_out, Opcode[4]);
  not not_8 (not_8_out, Opcode[3]);
  not not_9 (not_9_out, Opcode[6]);
  not not_10 (not_10_out, Opcode[4]);
  not not_11 (not_11_out, Opcode[3]);
  not not_12 (not_12_out, Opcode[4]);
  not not_13 (not_13_out, Opcode[2]);
  not not_14 (not_14_out, Opcode[3]);
  not not_15 (not_15_out, Opcode[4]);
  not not_16 (not_16_out, Opcode[5]);
  not not_17 (not_17_out, Opcode[6]);
  not not_18 (not_18_out, Opcode[2]);
  not not_19 (not_19_out, Opcode[3]);
  not not_20 (not_20_out, Opcode[5]);
  not not_21 (not_21_out, Opcode[6]);
  and and_1 (is_S, not_1_out, not_2_out, not_3_out, Opcode[5], not_4_out);
  and and_2 (B_010, not_5_out, not_6_out, not_7_out, Opcode[5], Opcode[6]);
  and and_3 (is_U, Opcode[2], not_8_out, Opcode[4], not_9_out);
  and and_4 (is_J, Opcode[2], Opcode[3], not_10_out, Opcode[5], Opcode[6]);
  and and_5 (is_jalr, Opcode[2], not_11_out, not_12_out, Opcode[5], Opcode[6]);
  and and_6 (is_I_load, not_13_out, not_14_out, not_15_out, not_16_out, not_17_out);
  and and_7 (is_I_load_or_IR, not_18_out, not_19_out, not_20_out, not_21_out);
  not not_22 (not_22_out, funct3[1]);
  and and_8 (and_8_out, funct3[0], not_22_out);
  not not_23 (not_23_out, and_8_out);
  not not_24 (not_24_out, funct3[1]);
  and and_9 (and_9_out, is_I_load_or_IR, not_23_out);
  and and_10 (and_10_out, funct3[0], not_24_out);
  and and_11 (IR_101, is_I_load_or_IR, and_10_out);
  or or_1 (I_000, is_jalr, is_I_load, and_9_out);
  Multiplexer #(.select(3), .width(3), .enable("false")) multiplexer_1 (
    .in0(3'b000), .in1(3'b001), .in2(3'b010), .in3(3'b101), .in4(3'b011), .in5(3'b100), .out(ImmSel),
    .sel(bitfinder_1_index));  // open: in6, in7
  BitFinder #(.width(6)) bitfinder_1 (
    .in({is_J, is_U, IR_101, B_010, is_S, I_000}), .index(bitfinder_1_index));  // open: found

  // Other names for the same wires on the sheet: S_001 = is_S; is_B = B_010; U_011 = is_U; J_100 = is_J

  // Notes on the sheet:
  //   INPUT
  //   OUTPUT
endmodule

module BrUn_processor (
  input  [6:0] Opcode,
  input  [2:0] funct3,
  output BrUn
);

  wire not_1_out, not_2_out, not_3_out;

  not not_1 (not_1_out, Opcode[2]);
  not not_2 (not_2_out, Opcode[3]);
  not not_3 (not_3_out, Opcode[4]);
  and and_1 (BrUn, not_1_out, not_2_out, not_3_out, Opcode[5], Opcode[6], funct3[1], funct3[2]);

  // Notes on the sheet:
  //   INPUT
  //   OUTPUT
endmodule

module ASel_processor (
  input  [6:0] Opcode,
  output ASel
);

  wire is_B, is_J, is_U, not_1_out, not_2_out, not_3_out, not_4_out, not_5_out, not_6_out;

  not not_1 (not_1_out, Opcode[2]);
  not not_2 (not_2_out, Opcode[3]);
  not not_3 (not_3_out, Opcode[4]);
  not not_4 (not_4_out, Opcode[4]);
  not not_5 (not_5_out, Opcode[3]);
  not not_6 (not_6_out, Opcode[6]);
  and and_1 (is_B, not_1_out, not_2_out, not_3_out, Opcode[5], Opcode[6]);
  and and_2 (is_J, Opcode[2], Opcode[3], not_4_out, Opcode[5], Opcode[6]);
  and and_3 (is_U, Opcode[2], not_5_out, Opcode[4], not_6_out);
  or or_1 (ASel, is_B, is_J, is_U);

  // Notes on the sheet:
  //   INPUT
  //   OUTPUT
endmodule

module BSel_processor (
  input  [6:0] Opcode,
  output BSel
);

  wire and_1_out, not_1_out, not_2_out, not_3_out;

  not not_1 (not_1_out, Opcode[2]);
  not not_2 (not_2_out, Opcode[3]);
  not not_3 (not_3_out, Opcode[6]);
  and and_1 (and_1_out, not_1_out, not_2_out, Opcode[4], Opcode[5], not_3_out);
  not not_4 (BSel, and_1_out);

  // Notes on the sheet:
  //   INPUT
  //   OUTPUT
endmodule

module ALUSel_processor (
  input  [6:0] Opcode,
  input  [2:0] funct3,
  input  [6:0] funct7,
  output [3:0] ALUSel
);

  wire Add_0000, And_0001, and_9_out, and_10_out, and_11_out, and_12_out, and_13_out, and_14_out, and_15_out,
       and_16_out, and_17_out, and_18_out, and_19_out, and_20_out, and_21_out, and_22_out, and_23_out,
       and_24_out, and_25_out, and_26_out, is_add, is_addi, is_and, is_andi, is_B, is_I_load, is_IR, is_J,
       is_jalr, is_or, is_R, is_S, is_set_less_than, is_set_less_than_unsigned_really, is_shift_left,
       is_shift_right, is_shift_right_arith, is_shift_right_really, is_sub, is_U, is_what, is_what1,
       is_what3, is_xor, not_1_out, not_2_out, not_3_out, not_4_out, not_5_out, not_6_out, not_7_out,
       not_8_out, not_9_out, not_10_out, not_11_out, not_12_out, not_13_out, not_14_out, not_15_out,
       not_16_out, not_17_out, not_18_out, not_19_out, not_20_out, not_21_out, not_22_out, not_23_out,
       not_24_out, not_25_out, not_26_out, not_27_out, not_28_out, not_29_out, not_30_out, not_31_out,
       not_32_out, not_33_out, not_34_out, not_35_out, not_36_out, not_37_out, not_38_out, not_39_out,
       not_40_out, not_41_out, not_42_out, not_43_out, not_44_out, not_45_out, not_46_out, not_47_out,
       not_48_out, not_49_out, not_50_out, not_51_out, not_52_out, not_53_out, not_54_out, not_55_out,
       or_1_out, or_2_out, or_3_out, or_4_out, or_5_out, or_6_out;
  wire [3:0] bitfinder_1_index;

  not not_1 (not_1_out, Opcode[2]);
  not not_2 (not_2_out, Opcode[3]);
  not not_3 (not_3_out, Opcode[4]);
  not not_4 (not_4_out, Opcode[4]);
  not not_5 (not_5_out, Opcode[3]);
  not not_6 (not_6_out, Opcode[6]);
  not not_7 (not_7_out, Opcode[3]);
  not not_8 (not_8_out, Opcode[4]);
  not not_9 (not_9_out, Opcode[2]);
  not not_10 (not_10_out, Opcode[3]);
  not not_11 (not_11_out, Opcode[4]);
  not not_12 (not_12_out, Opcode[6]);
  not not_13 (not_13_out, Opcode[2]);
  not not_14 (not_14_out, Opcode[3]);
  not not_15 (not_15_out, Opcode[4]);
  not not_16 (not_16_out, Opcode[5]);
  not not_17 (not_17_out, Opcode[6]);
  not not_18 (not_18_out, Opcode[2]);
  not not_19 (not_19_out, Opcode[3]);
  not not_20 (not_20_out, Opcode[5]);
  not not_21 (not_21_out, Opcode[6]);
  not not_22 (not_22_out, Opcode[2]);
  not not_23 (not_23_out, Opcode[3]);
  not not_24 (not_24_out, Opcode[6]);
  and and_1 (is_B, not_1_out, not_2_out, not_3_out, Opcode[5], Opcode[6]);
  and and_2 (is_J, Opcode[2], Opcode[3], not_4_out, Opcode[5], Opcode[6]);
  and and_3 (is_U, Opcode[2], not_5_out, Opcode[4], not_6_out);
  and and_4 (is_jalr, Opcode[2], not_7_out, not_8_out, Opcode[5], Opcode[6]);
  and and_5 (is_S, not_9_out, not_10_out, not_11_out, Opcode[5], not_12_out);
  and and_6 (is_I_load, not_13_out, not_14_out, not_15_out, not_16_out, not_17_out);
  and and_7 (is_IR, not_18_out, not_19_out, Opcode[4], not_20_out, not_21_out);
  and and_8 (is_R, not_22_out, not_23_out, Opcode[4], Opcode[5], not_24_out);
  not not_25 (not_25_out, funct3[0]);
  not not_26 (not_26_out, funct3[1]);
  not not_27 (not_27_out, funct3[2]);
  not not_28 (not_28_out, funct3[0]);
  not not_29 (not_29_out, funct3[1]);
  not not_30 (not_30_out, funct3[2]);
  not not_31 (not_31_out, funct7[0]);
  not not_32 (not_32_out, funct7[5]);
  not not_33 (not_33_out, funct7[0]);
  not not_34 (not_34_out, funct3[0]);
  not not_35 (not_35_out, funct3[0]);
  not not_36 (not_36_out, funct3[1]);
  not not_37 (not_37_out, funct3[1]);
  not not_38 (not_38_out, funct7[0]);
  not not_39 (not_39_out, funct7[5]);
  not not_40 (not_40_out, funct3[1]);
  not not_41 (not_41_out, funct3[1]);
  not not_42 (not_42_out, funct3[2]);
  not not_43 (not_43_out, funct7[0]);
  not not_44 (not_44_out, funct3[0]);
  not not_45 (not_45_out, funct3[2]);
  and and_9 (and_9_out, not_25_out, not_26_out, not_27_out);
  and and_10 (and_10_out, not_28_out, not_29_out, not_30_out);
  and and_11 (and_11_out, not_31_out, not_32_out);
  and and_12 (and_12_out, funct3[0], funct3[1], funct3[2]);
  and and_13 (and_13_out, funct3[0], funct3[1], funct3[2]);
  or or_1 (or_1_out, is_IR, is_R);
  and and_14 (and_14_out, not_34_out, funct3[1], funct3[2]);
  or or_2 (or_2_out, is_IR, is_R);
  and and_15 (and_15_out, not_35_out, not_36_out, funct3[2]);
  or or_3 (or_3_out, is_IR, is_R);
  and and_16 (and_16_out, funct3[0], not_37_out, funct3[2]);
  and and_17 (and_17_out, not_38_out, not_39_out);
  or or_4 (or_4_out, is_IR, is_R);
  and and_18 (and_18_out, funct3[0], not_40_out, funct3[2]);
  or or_5 (or_5_out, is_IR, is_R);
  and and_19 (and_19_out, funct3[0], not_41_out, not_42_out);
  or or_6 (or_6_out, is_IR, is_R);
  and and_20 (and_20_out, not_44_out, funct3[1], not_45_out);
  not not_46 (not_46_out, funct3[1]);
  and and_21 (and_21_out, funct3[0], not_46_out, funct3[2]);
  and and_22 (and_22_out, funct3[0], funct3[1], funct3[2]);
  not not_47 (not_47_out, funct3[0]);
  and and_23 (and_23_out, not_47_out, not_48_out, not_49_out);
  not not_48 (not_48_out, funct3[1]);
  not not_49 (not_49_out, funct3[2]);
  and and_24 (and_24_out, funct3[0], funct3[1], not_50_out);
  not not_50 (not_50_out, funct3[2]);
  not not_51 (not_51_out, funct3[0]);
  and and_25 (and_25_out, not_51_out, not_52_out, not_53_out);
  not not_52 (not_52_out, funct3[1]);
  not not_53 (not_53_out, funct3[2]);
  not not_54 (not_54_out, funct3[1]);
  and and_26 (and_26_out, funct3[0], not_54_out, not_55_out);
  not not_55 (not_55_out, funct3[2]);
  and and_27 (is_addi, is_IR, and_9_out);
  and and_28 (is_add, is_R, and_10_out, and_11_out);
  and and_29 (is_andi, is_IR, and_12_out);
  and and_30 (is_and, is_R, and_13_out, not_33_out);
  and and_31 (is_or, or_1_out, and_14_out);
  and and_32 (is_xor, or_2_out, and_15_out);
  and and_33 (is_shift_right, or_3_out, and_16_out, and_17_out);
  and and_34 (is_shift_right_arith, or_4_out, and_18_out, funct7[5]);
  and and_35 (is_shift_left, or_5_out, and_19_out, not_43_out);
  and and_36 (is_set_less_than, or_6_out, and_20_out);
  and and_37 (is_shift_right_really, is_R, and_21_out, funct7[0]);
  and and_38 (is_what, is_R, and_22_out, funct7[0]);
  and and_39 (is_what1, is_R, and_23_out, funct7[0]);
  and and_40 (is_set_less_than_unsigned_really, is_R, and_24_out, funct7[0]);
  and and_41 (is_sub, is_R, and_25_out, funct7[5]);
  and and_42 (is_what3, is_R, and_26_out, funct7[0]);
  or or_7 (Add_0000, is_B, is_J, is_U, is_jalr, is_addi, is_add, is_S, is_I_load);
  or or_8 (And_0001, is_andi, is_and);
  Multiplexer #(.select(4), .width(4), .enable("false")) multiplexer_1 (
    .in0(4'b0000), .in1(4'b0001), .in2(4'b0010), .in3(4'b0011), .in4(4'b0100), .in5(4'b0101), .in6(4'b0110),
    .in7(4'b0111), .in8(4'b1000), .in9(4'b1001), .in10(4'b1010), .in11(4'b1011), .in12(4'b1100),
    .in13(4'b1110), .out(ALUSel), .sel(bitfinder_1_index));  // open: in14, in15
  BitFinder #(.width(14)) bitfinder_1 (
    .in({is_what3, is_sub, is_set_less_than_unsigned_really, is_what1, is_what, is_shift_right_really, is_set_less_than, is_shift_left, is_shift_right_arith, is_shift_right, is_xor, is_or, And_0001, Add_0000}),
    .index(bitfinder_1_index));  // open: found

  // Other names for the same wires on the sheet: OR_0010 = is_or; XOR_0011 = is_xor; SR_0100 = is_shift_right;
  //   SRA_0101 = is_shift_right_arith; SLL_0110 = is_shift_left; SLT_0111 = is_set_less_than;
  //   SRR_1000 = is_shift_right_really; WHAT_1001 = is_what; WHAT1_1010 = is_what1;
  //   SLTUR_1011 = is_set_less_than_unsigned_really; SUB_1100 = is_sub; WHAT3_1110 = is_what3

  // Notes on the sheet:
  //   INPUT
  //   OUTPUT
endmodule

module MemRW_processor (
  input  [6:0] Opcode,
  input  [2:0] funct3,
  input  BrEq,
  input  BrLt,
  output MemRW
);

  wire is_S, is_sw, is_what, not_1_out, not_2_out, not_3_out, not_4_out, not_5_out, not_6_out, not_7_out,
       or_1_out;

  not not_1 (not_1_out, Opcode[2]);
  not not_2 (not_2_out, Opcode[3]);
  not not_3 (not_3_out, Opcode[4]);
  not not_4 (not_4_out, Opcode[6]);
  not not_5 (not_5_out, funct3[0]);
  not not_6 (not_6_out, funct3[2]);
  not not_7 (not_7_out, BrEq);
  and and_1 (is_S, not_1_out, not_2_out, not_3_out, Opcode[5], not_4_out);
  and and_2 (is_sw, not_5_out, funct3[1], not_6_out);
  and and_3 (is_what, funct3[0], funct3[1], funct3[2], not_7_out, BrLt);
  or or_1 (or_1_out, is_sw, is_what);
  and and_4 (MemRW, is_S, or_1_out);

  // Notes on the sheet:
  //   INPUT
  //   OUTPUT
endmodule

module WBSel_processor (
  input  [6:0] Opcode,
  input  [2:0] funct3,
  output [1:0] WBSel
);

  wire is_auipc, is_I_load, is_IR, is_J, is_jalr, is_lui, is_R, not_1_out, not_2_out, not_3_out, not_4_out,
       not_5_out, not_6_out, not_7_out, not_8_out, not_9_out, not_10_out, not_11_out, not_12_out, not_13_out,
       not_14_out, not_15_out, not_16_out, not_17_out, not_18_out, not_19_out, not_20_out, OUT01_ALU,
       OUT10_PC_4;
  wire [1:0] bitfinder_1_index;

  not not_1 (not_1_out, Opcode[2]);
  not not_2 (not_2_out, Opcode[3]);
  not not_3 (not_3_out, Opcode[6]);
  not not_4 (not_4_out, Opcode[2]);
  not not_5 (not_5_out, Opcode[3]);
  not not_6 (not_6_out, Opcode[5]);
  not not_7 (not_7_out, Opcode[6]);
  not not_8 (not_8_out, Opcode[3]);
  not not_9 (not_9_out, Opcode[5]);
  not not_10 (not_10_out, Opcode[6]);
  not not_11 (not_11_out, Opcode[4]);
  not not_12 (not_12_out, Opcode[2]);
  not not_13 (not_13_out, Opcode[3]);
  not not_14 (not_14_out, Opcode[4]);
  not not_15 (not_15_out, Opcode[5]);
  not not_16 (not_16_out, Opcode[6]);
  not not_17 (not_17_out, Opcode[3]);
  not not_18 (not_18_out, Opcode[6]);
  not not_19 (not_19_out, Opcode[3]);
  not not_20 (not_20_out, Opcode[4]);
  and and_1 (is_R, not_1_out, not_2_out, Opcode[4], Opcode[5], not_3_out);
  and and_2 (is_IR, not_4_out, not_5_out, Opcode[4], not_6_out, not_7_out);
  and and_3 (is_auipc, Opcode[2], not_8_out, Opcode[4], not_9_out, not_10_out);
  and and_4 (is_J, Opcode[2], Opcode[3], not_11_out, Opcode[5], Opcode[6]);
  and and_5 (is_I_load, not_12_out, not_13_out, not_14_out, not_15_out, not_16_out);
  and and_6 (is_lui, Opcode[2], not_17_out, Opcode[4], Opcode[5], not_18_out);
  and and_7 (is_jalr, Opcode[2], not_19_out, not_20_out, Opcode[5], Opcode[6]);
  or or_1 (OUT01_ALU, is_R, is_auipc, is_IR);
  or or_2 (OUT10_PC_4, is_J, is_jalr);
  Multiplexer #(.select(2), .width(2), .enable("false")) multiplexer_1 (
    .in0(2'b00), .in1(2'b01), .in2(2'b10), .in3(2'b11), .out(WBSel), .sel(bitfinder_1_index));
  BitFinder #(.width(4)) bitfinder_1 (
    .in({is_lui, OUT10_PC_4, OUT01_ALU, is_I_load}), .index(bitfinder_1_index));  // open: found

  // Other names for the same wires on the sheet: OUT00_Mem = is_I_load; OUT11_NOPE = is_lui

  // Notes on the sheet:
  //   INPUT
  //   OUTPUT
endmodule

module BrSel_processor (
  input  [6:0] Opcode,
  input  [2:0] funct3,
  output BrSel
);

  wire not_1_out, not_2_out, not_3_out, not_4_out;

  not not_1 (not_1_out, Opcode[2]);
  not not_2 (not_2_out, Opcode[3]);
  not not_3 (not_3_out, Opcode[4]);
  not not_4 (not_4_out, Opcode[6]);
  and and_1 (BrSel, not_1_out, not_2_out, not_3_out, Opcode[5], not_4_out);

  // Other names for the same wires on the sheet: is_S = BrSel

  // Notes on the sheet:
  //   INPUT
  //   OUTPUT
endmodule

module AddrSel_processor (
  input  [6:0] Opcode,
  input  [2:0] funct3,
  input  BrEq,
  input  BrLt,
  output AddrSel
);

  wire and_1_out, and_2_out, is_S, not_1_out, not_2_out, not_3_out, not_4_out, not_5_out;

  not not_1 (not_1_out, BrEq);
  not not_2 (not_2_out, Opcode[2]);
  not not_3 (not_3_out, Opcode[3]);
  not not_4 (not_4_out, Opcode[4]);
  not not_5 (not_5_out, Opcode[6]);
  and and_1 (and_1_out, funct3[0], funct3[1], funct3[2]);
  and and_2 (and_2_out, not_1_out, BrLt);
  and and_3 (is_S, not_2_out, not_3_out, not_4_out, Opcode[5], not_5_out);
  and and_4 (AddrSel, is_S, and_1_out, and_2_out);

  // Notes on the sheet:
  //   INPUT
  //   OUTPUT
endmodule
