// Logisim project cpu.circ as structural Verilog: 2 circuits, main circuit main
module main (
  input  [31:0] INSTRUCTION,
  input  CLOCK,
  output [31:0] PROGRAM_COUNTER,
  output [31:0] ra,
  output [31:0] sp,
  output [31:0] t0,
  output [31:0] t1,
  output [31:0] t2,
  output [31:0] s0,
  output [31:0] s1,
  output [31:0] a0
);

  wire AddrSel, ASel, BrEq, BrLt, BrSel, BrUn, BSel, MemRW, PCSel, RegWEn;
  wire [1:0] WBSel;
  wire [2:0] func3, ImmSel;
  wire [3:0] ALUSel;
  wire [31:0] alu_out, atomic_write_address, data_read_from_DMEM, imm, INSTRUCTION_OUT, multiplexer_1_out,
       multiplexer_2_out, multiplexer_4_out, multiplexer_5_out, multiplexer_6_out, PC_plus_4, PC_VALUE,
       PC_VALUE_plus_4, processed_read_data, read_address, read_or_write_address, rs2_out, wb;

  control_logic control_logic_1 (
    .BSel(BSel), .ImmSel(ImmSel), .BrLt(BrLt), .BrUn(BrUn), .RegWEn(RegWEn), .ASel(ASel), .PCSel(PCSel),
    .BrEq(BrEq), .inst({INSTRUCTION_OUT[31:15], func3, INSTRUCTION_OUT[11:0]}), .ALUSel(ALUSel),
    .MemRW(MemRW), .WBSel(WBSel), .AddrSel(AddrSel), .BrSel(BrSel));
  Multiplexer #(.width(32), .enable("false")) multiplexer_1 (
    .in0(PC_plus_4), .in1(alu_out), .out(multiplexer_1_out), .sel(PCSel));
  Adder #(.width(32)) adder_1 (.a(PROGRAM_COUNTER), .b(32'h4), .out(PC_plus_4));  // open: cin, cout
  Register #(.width(32)) PC (.D(multiplexer_1_out), .clk(CLOCK), .Q(PROGRAM_COUNTER));  // open: en, clr
  imm_gen imm_gen_1 (.ImmSel(ImmSel), .inst({INSTRUCTION_OUT[31:15], func3, INSTRUCTION_OUT[11:0]}), .imm(imm));
  Register #(.width(32)) register_1 (.D(PROGRAM_COUNTER), .clk(CLOCK), .Q(PC_VALUE));  // open: en, clr
  Multiplexer #(.width(32), .enable("false")) multiplexer_2 (
    .in0(rs2_out), .in1(imm), .out(multiplexer_2_out), .sel(BrSel));
  after_DMEM after_dmem_1 (
    .ReadAddr(read_address), .func3(func3), .data_read_from_DMEM(data_read_from_DMEM),
    .processed_read_data(processed_read_data));
  branch_comp branch_comp_1 (
    .BrEq(BrEq), .BrUn(BrUn), .rs1(atomic_write_address), .BrLt(BrLt), .rs2(multiplexer_2_out));
  Multiplexer #(.width(32), .enable("false")) multiplexer_3 (
    .in0(alu_out), .in1(atomic_write_address), .out(read_or_write_address), .sel(AddrSel));
  Adder #(.width(32)) adder_2 (.a(PC_VALUE), .b(32'h4), .out(PC_VALUE_plus_4));  // open: cin, cout
  regfile_main RegFile (
    .rs2(INSTRUCTION_OUT[24:20]), .rd(INSTRUCTION_OUT[11:7]), .Read_Data_1(atomic_write_address),
    .Read_Data_2(rs2_out), .ra(ra), .sp(sp), .t0(t0), .t1(t1), .t2(t2), .s0(s0), .s1(s1), .a0(a0),
    .rs1(INSTRUCTION_OUT[19:15]), .Write_Data(wb), .RegWEn(RegWEn), .clk(CLOCK));
  Multiplexer #(.width(32), .enable("false")) multiplexer_4 (
    .in0(INSTRUCTION), .in1(32'h13), .out(multiplexer_4_out), .sel(PCSel));
  Multiplexer #(.width(32), .enable("false")) multiplexer_5 (
    .in0(atomic_write_address), .in1(PC_VALUE), .out(multiplexer_5_out), .sel(ASel));
  Multiplexer #(.width(32), .enable("false")) multiplexer_6 (
    .in0(rs2_out), .in1(imm), .out(multiplexer_6_out), .sel(BSel));
  Register #(.width(32)) register_2 (
    .D(multiplexer_4_out), .clk(CLOCK), .Q({INSTRUCTION_OUT[31:15], func3, INSTRUCTION_OUT[11:0]}));  // open: en, clr
  alu Arithmetic_Logic_Unit (.Result(alu_out), .ALUSel(ALUSel), .A(multiplexer_5_out), .B(multiplexer_6_out));
  Multiplexer #(.select(2), .width(32), .enable("false")) multiplexer_7 (
    .in0(processed_read_data), .in1(alu_out), .in2(PC_VALUE_plus_4), .in3(imm), .out(wb), .sel(WBSel));
  // mem_main DMEM: pin names not known; wires that end beside it: read_or_write_address, rs2_out, CLOCK, MemRW, data_read_from_DMEM

  // Other names for the same wires on the sheet: clk = CLOCK; rd_in[4:0] = INSTRUCTION_OUT[11:7];
  //   INSTRUCTION_OUT[14:12] = func3; rs1_in[4:0] = INSTRUCTION_OUT[19:15]; rs2_in[4:0] = INSTRUCTION_OUT[24:20];
  //   read_normal_write_address[31:0] = alu_out; rs1_out[31:0] = atomic_write_address

  // Notes on the sheet:
  //   Output
  //   IMEM (do **NOT** move this)
  //   Inputs
  //   It is OK to move the PC, RegFile, ALU, MEM, Branch Comp, Imm Gen, and Control Logic to wherever is most convenient for you when constructing your CPU, and to delete this text
  //   Inputs/Outputs for testing. Do **NOT** move these.
endmodule

module after_DMEM (
  input  [31:0] ReadAddr,
  input  [2:0] func3,
  input  [31:0] data_read_from_DMEM,
  output [31:0] processed_read_data
);

  wire [31:0] lb, lh;

  Multiplexer #(.select(2), .width(32), .enable("false")) multiplexer_1 (
    .in0({{25{data_read_from_DMEM[7]}}, data_read_from_DMEM[6:0]}),
    .in1({{25{data_read_from_DMEM[15]}}, data_read_from_DMEM[14:8]}),
    .in2({{25{data_read_from_DMEM[23]}}, data_read_from_DMEM[22:16]}),
    .in3({{25{data_read_from_DMEM[31]}}, data_read_from_DMEM[30:24]}), .out(lb), .sel(ReadAddr[1:0]));
  Multiplexer #(.width(32), .enable("false")) multiplexer_2 (
    .in0({{17{data_read_from_DMEM[15]}}, data_read_from_DMEM[14:0]}),
    .in1({{17{data_read_from_DMEM[31]}}, data_read_from_DMEM[30:16]}), .out(lh), .sel(ReadAddr[1]));
  Multiplexer #(.select(3), .width(32), .enable("false")) multiplexer_3 (
    .in0(lb), .in1(lh), .in2(data_read_from_DMEM), .out(processed_read_data), .sel(func3));  // open: in3, in4, in5, in6, in7

  // Other names for the same wires on the sheet: byte1[31:0] = {{25{data_read_from_DMEM[15]}}, data_read_from_DMEM[14:8]};
  //   half0[31:0] = {{17{data_read_from_DMEM[15]}}, data_read_from_DMEM[14:0]}; lw[31:0] = data_read_from_DMEM;
  //   byte2[31:0] = {{25{data_read_from_DMEM[23]}}, data_read_from_DMEM[22:16]};
  //   half1[31:0] = {{17{data_read_from_DMEM[31]}}, data_read_from_DMEM[30:16]};
  //   byte3[31:0] = {{25{data_read_from_DMEM[31]}}, data_read_from_DMEM[30:24]};
  //   byte0[31:0] = {{25{data_read_from_DMEM[7]}}, data_read_from_DMEM[6:0]}
endmodule
