// Logisim project imm_gen.circ as structural Verilog: 1 circuit, main circuit imm_gen
module imm_gen (
  input  [31:0] inst,
  input  [2:0] ImmSel,
  output [31:0] imm
);

  Multiplexer #(.select(3), .width(32), .enable("false")) multiplexer_1 (
    .in0({{21{inst[31]}}, inst[30:20]}), .in1({{21{inst[31]}}, inst[30:25], inst[11:7]}),
    .in2({{20{inst[31]}}, inst[7], inst[30:25], inst[11:8], 1'b0}), .in3({inst[31:12], {12{1'b0}}}),
    .in4({{12{inst[31]}}, inst[19:12], inst[20], inst[30:25], inst[11:8], 1'b0}),
    .in5({{28{inst[24]}}, inst[23:20]}), .out(imm), .sel(ImmSel));  // open: in6, in7

  // Other names for the same wires on the sheet: imm_I[31:0] = {{21{inst[31]}}, inst[30:20]};
  //   imm_IR[31:0] = {{28{inst[24]}}, inst[23:20]}; imm_U[31:12] = inst[31:12];
  //   imm_UJ[31:1] = {{12{inst[31]}}, inst[19:12], inst[20], inst[30:25], inst[11:8]};
  //   imm_S[31:0] = {{21{inst[31]}}, inst[30:25], inst[11:7]};
  //   imm_SB[31:1] = {{20{inst[31]}}, inst[7], inst[30:25], inst[11:8]}

  // Notes on the sheet:
  //   INPUTS to your circuit
  //   DON'T CHANGE THE LOCATIONS OF THE INPUTS AND OUTPUTS!
  //   OUTPUT from your circuit
endmodule
